// Logisim project logic.circ as structural Verilog: 1 circuit, main circuit main
module main (
  input  in_1,
  input  in_2,
  input  in_3,
  input  in_4,
  input  in_5,
  input  in_6,
  input  in_7,
  input  in_8,
  input  in_9,
  input  in_10,
  input  in_11,
  input  i_o_m
);

  wire and_1_out, and_2_out, and_3_out, and_4_out, n7400_1_pin8, n7400_1_pin9, n7400_1_pin10, n7400_1_pin11,
       n7404_1_pin10, n7404_1_pin12, n7408_1_pin1, n7408_1_pin2, nand_1_out, nand_2_out, not_1_out, not_2_out;

  _7404 u_7404_1 (
    .pin13(in_7), .pin12(n7404_1_pin12), .pin11(i_o_m), .pin10(n7404_1_pin10));  // open: pin1, pin2, pin3, pin4, pin5, pin6, pin9, pin8
  not not_1 (not_1_out, in_1);
  not not_2 (not_2_out, in_2);
  and and_1 (and_1_out, in_3, in_4);
  and and_2 (and_2_out, in_5, in_6);
  _7400 u_7400_1 (
    .pin13(n7404_1_pin12), .pin12(n7404_1_pin10), .pin11(n7400_1_pin11), .pin10(n7400_1_pin10),
    .pin9(n7400_1_pin9), .pin8(n7400_1_pin8));  // open: pin1, pin2, pin3, pin4, pin5, pin6
  and and_3 (and_3_out, not_1_out, in_2);
  and and_4 (and_4_out, and_1_out, and_2_out);
  nand nand_1 (nand_1_out, not_1_out, not_2_out);
  nand nand_2 (nand_2_out, and_3_out, and_4_out);
  _7408 u_7408_1 (
    .pin1(n7408_1_pin1), .pin2(n7408_1_pin2), .pin3(n7400_1_pin9), .pin4(in_10), .pin5(in_11),
    .pin6(n7408_1_pin2), .pin13(n7404_1_pin10), .pin12(in_7), .pin11(n7400_1_pin10), .pin10(in_8),
    .pin9(in_9), .pin8(n7408_1_pin1));
  // Probe on n7400_1_pin11
  // Probe on n7400_1_pin8

  // Notes on the sheet:
  //   19    18   17  16  15
  //   ram
  //   rom
  //   ram
  //   rom
endmodule
